// Logisim project FAS7.circ as structural Verilog: 11 circuits, main circuit Adder
// ADDER-SUBTRACOTR
module Adder (
  input  B,
  input  A,
  input  Ci,
  output COUT,
  output Sum
);

  wire and_1_out, and_2_out, xor_1_out;

  and and_1 (and_1_out, B, A);
  and and_2 (and_2_out, xor_1_out, Ci);
  or or_1 (COUT, and_1_out, and_2_out);
  xor xor_1 (xor_1_out, B, A);
  xor xor_2 (Sum, xor_1_out, Ci);
endmodule

module adder_sub (
  input  B4,
  input  A4,
  input  B3,
  input  A3,
  input  B2,
  input  A2,
  input  B1,
  input  A1,
  input  B0,
  input  A0,
  input  Ci,
  output COUT,
  output OUT0,
  output OUT4,
  output OUT3,
  output OUT2,
  output OUT1
);

  wire adder_2_cout, adder_3_cout, adder_4_cout, adder_5_cout, xor_1_out, xor_2_out, xor_3_out, xor_4_out,
       xor_5_out;

  xor xor_1 (xor_1_out, B4, Ci);
  Adder adder_1 (.COUT(COUT), .B(xor_1_out), .A(A4), .Sum(OUT4), .Ci(adder_2_cout));
  xor xor_2 (xor_2_out, B3, Ci);
  Adder adder_2 (.COUT(adder_2_cout), .B(xor_2_out), .A(A3), .Sum(OUT3), .Ci(adder_3_cout));
  xor xor_3 (xor_3_out, B2, Ci);
  Adder adder_3 (.COUT(adder_3_cout), .B(xor_3_out), .A(A2), .Sum(OUT2), .Ci(adder_4_cout));
  xor xor_4 (xor_4_out, B1, Ci);
  Adder adder_4 (.COUT(adder_4_cout), .B(xor_4_out), .A(A1), .Sum(OUT1), .Ci(adder_5_cout));
  xor xor_5 (xor_5_out, B0, Ci);
  Adder adder_5 (.COUT(adder_5_cout), .B(xor_5_out), .A(A0), .Sum(OUT0), .Ci(Ci));
endmodule

module FINAL (
  input  B4,
  input  B3,
  input  B2,
  input  B1,
  input  B0,
  input  A0,
  input  A1,
  input  A2,
  input  A3,
  input  A4,
  input  S1,
  input  S0,
  output Y0,
  output OUTPUT_ZERO,
  output Y1,
  output Cout,
  output OUTPUT_negative,
  output Y2,
  output Y3,
  output A__B,
  output Y4,
  output A__B_2,
  output Y5,
  output Y6,
  output Y7,
  output Y8,
  output Y9
);

  wire Adder_subtractor_out0, Adder_subtractor_out1, Adder_subtractor_out2, Adder_subtractor_out3,
       Adder_subtractor_out4, comparator_output_is_negative, Multiplier_out_0, Multiplier_out_1,
       Multiplier_out_2, Multiplier_out_3, Multiplier_out_4, Multiplier_out_5, Multiplier_out_6,
       Multiplier_out_7, Multiplier_out_8, Multiplier_out_9, Multiplier_zero, nor_1_out, not_1_out0,
       not_1_out1, not_1_out2, not_1_out3, not_1_out4, not_1_zero, Small_decoder_mux0, Small_decoder_mux1;

  multiblair Multiplier (
    .B0(B0), .B1(B1), .B2(B2), .B3(B3), .B4(B4), .A4(A4), .A3(A3), .A2(A2), .A1(A1), .A0(A0),
    .Out_9(Multiplier_out_9), .Out_8(Multiplier_out_8), .Out_7(Multiplier_out_7), .Out_6(Multiplier_out_6),
    .Out_5(Multiplier_out_5), .Out_4(Multiplier_out_4), .ZERO(Multiplier_zero), .Out_3(Multiplier_out_3),
    .Out_2(Multiplier_out_2), .Out_1(Multiplier_out_1), .Out_0(Multiplier_out_0));
  NOT not_1 (
    .A0(A0), .A1(A1), .A2(A2), .A3(A3), .A4(A4), .OUT0(not_1_out0), .OUT1(not_1_out1), .OUT2(not_1_out2),
    .OUT3(not_1_out3), .OUT4(not_1_out4), .ZERO(not_1_zero));
  adder_sub Adder_subtractor (
    .COUT(Cout), .Ci(S0), .B4(B4), .A4(A4), .B3(B3), .A3(A3), .B2(B2), .A2(A2), .B1(B1), .A1(A1), .B0(B0),
    .A0(A0), .OUT4(Adder_subtractor_out4), .OUT3(Adder_subtractor_out3), .OUT2(Adder_subtractor_out2),
    .OUT1(Adder_subtractor_out1), .OUT0(Adder_subtractor_out0));
  nor nor_1 (nor_1_out, Adder_subtractor_out0, Adder_subtractor_out1, Adder_subtractor_out2, Adder_subtractor_out3, Adder_subtractor_out4);
  and and_1 (OUTPUT_negative, Small_decoder_mux0, comparator_output_is_negative);
  combare comparator (
    .A__B(A__B_2), .Output_is_negative(comparator_output_is_negative), .A4(A4), .A3(A3), .A2(A2), .A1(A1),
    .A0(A0), .B0(B0), .B1(B1), .B2(B2), .B3(B3), .B4(B4), .A__B_2(A__B));
  trans_mux trans_mux_1 (
    .D0(nor_1_out), .D1(nor_1_out), .D2(Multiplier_zero), .D3(not_1_zero), .S1(S1), .S0(S0),
    .OUTPUT(OUTPUT_ZERO));
  SMALL_mux Small_decoder (.mux1(Small_decoder_mux1), .mux0(Small_decoder_mux0), .S1(S1), .S0(S0));
  trans_mux trans_mux_2 (
    .D0(Adder_subtractor_out0), .D1(Adder_subtractor_out0), .D2(Multiplier_out_0), .D3(not_1_out0), .S1(S1),
    .S0(S0), .OUTPUT(Y0));
  trans_mux trans_mux_3 (
    .D0(Adder_subtractor_out1), .D1(Adder_subtractor_out1), .D2(Multiplier_out_1), .D3(not_1_out1), .S1(S1),
    .S0(S0), .OUTPUT(Y1));
  trans_mux trans_mux_4 (
    .D0(Adder_subtractor_out2), .D1(Adder_subtractor_out2), .D2(Multiplier_out_2), .D3(not_1_out2), .S1(S1),
    .S0(S0), .OUTPUT(Y2));
  trans_mux trans_mux_5 (
    .D0(Adder_subtractor_out3), .D1(Adder_subtractor_out3), .D2(Multiplier_out_3), .D3(not_1_out3), .S1(S1),
    .S0(S0), .OUTPUT(Y3));
  trans_mux trans_mux_6 (
    .D0(Adder_subtractor_out4), .D1(Adder_subtractor_out4), .D2(Multiplier_out_4), .D3(not_1_out4), .S1(S1),
    .S0(S0), .OUTPUT(Y4));
  MUX_and small_mux (
    .A0(Multiplier_out_5), .A1(Multiplier_out_6), .A2(Multiplier_out_7), .A3(Multiplier_out_8),
    .A4(Multiplier_out_9), .S(Small_decoder_mux1), .out_7(Y5), .out_8(Y6), .out_9(Y7), .out_10(Y8),
    .out_11(Y9));
endmodule

module MUX (
  input  A0,
  input  A1,
  input  A2,
  input  A3,
  input  S3,
  input  S2,
  input  S1,
  input  S0,
  output OUTPUT
);

  wire and_1_out, and_2_out, and_3_out, and_4_out;

  and and_1 (and_1_out, A0, S0);
  and and_2 (and_2_out, A1, S1);
  and and_3 (and_3_out, A2, S2);
  and and_4 (and_4_out, A3, S3);
  or or_1 (OUTPUT, and_1_out, and_2_out, and_3_out, and_4_out);
endmodule

module NOT (
  input  A0,
  input  A1,
  input  A2,
  input  A3,
  input  A4,
  output OUT0,
  output OUT1,
  output OUT2,
  output OUT3,
  output OUT4,
  output ZERO
);

  not not_1 (OUT0, A0);
  not not_2 (OUT1, A1);
  not not_3 (OUT2, A2);
  not not_4 (OUT3, A3);
  not not_5 (OUT4, A4);
  nor nor_1 (ZERO, OUT0, OUT1, OUT2, OUT3, OUT4);
endmodule

module MUX_and (
  input  A0,
  input  A1,
  input  A2,
  input  A3,
  input  A4,
  input  S,
  output out_7,
  output out_8,
  output out_9,
  output out_10,
  output out_11
);

  and and_1 (out_7, A0, S);
  and and_2 (out_8, A1, S);
  and and_3 (out_9, A2, S);
  and and_4 (out_10, S, A3);
  and and_5 (out_11, A4, S);
endmodule

// Multiplier
module add_mult (
  input  B0,
  input  A0,
  input  S0,
  input  B3,
  input  A3,
  input  S3,
  input  B2,
  input  A2,
  input  S2,
  input  B1,
  input  A1,
  input  S1,
  input  B4,
  input  A4,
  input  S4,
  input  C0,
  input  C3,
  input  C2,
  input  C1,
  input  C4,
  output COUT0,
  output COUT3,
  output COUT2,
  output COUT1,
  output COUT4,
  output OUT0,
  output OUT3,
  output OUT2,
  output OUT1,
  output OUT4
);

  wire and_1_out, and_2_out, and_3_out, and_4_out, and_5_out;

  and and_1 (and_1_out, B4, A4);
  Adder adder_1 (.COUT(COUT4), .B(and_1_out), .A(S4), .Sum(OUT4), .Ci(C4));
  and and_2 (and_2_out, B3, A3);
  Adder adder_2 (.COUT(COUT3), .B(and_2_out), .A(S3), .Sum(OUT3), .Ci(C3));
  and and_3 (and_3_out, B2, A2);
  Adder adder_3 (.COUT(COUT2), .B(and_3_out), .A(S2), .Sum(OUT2), .Ci(C2));
  and and_4 (and_4_out, B1, A1);
  Adder adder_4 (.COUT(COUT1), .B(and_4_out), .A(S1), .Sum(OUT1), .Ci(C1));
  and and_5 (and_5_out, B0, A0);
  Adder adder_5 (.COUT(COUT0), .B(and_5_out), .A(S0), .Sum(OUT0), .Ci(C0));
endmodule

module multiblair (
  input  A4,
  input  A3,
  input  A2,
  input  A1,
  input  A0,
  input  B0,
  input  B1,
  input  B2,
  input  B3,
  input  B4,
  output Out_0,
  output Out_3,
  output Out_2,
  output Out_1,
  output Out_7,
  output Out_9,
  output Out_8,
  output Out_6,
  output Out_5,
  output Out_4,
  output ZERO
);

  wire add_mult_1_cout0, add_mult_1_cout1, add_mult_1_cout2, add_mult_1_cout3, add_mult_1_cout4,
       add_mult_1_out1, add_mult_1_out2, add_mult_1_out3, add_mult_1_out4, add_mult_2_cout0,
       add_mult_2_cout1, add_mult_2_cout2, add_mult_2_cout3, add_mult_2_cout4, add_mult_2_out1,
       add_mult_2_out2, add_mult_2_out3, add_mult_2_out4, add_mult_3_cout0, add_mult_3_cout1,
       add_mult_3_cout2, add_mult_3_cout3, add_mult_3_cout4, add_mult_3_out1, add_mult_3_out2,
       add_mult_3_out3, add_mult_3_out4, add_mult_4_cout0, add_mult_4_cout1, add_mult_4_cout2,
       add_mult_4_cout3, add_mult_4_cout4, add_mult_4_out1, add_mult_4_out2, add_mult_4_out3,
       add_mult_4_out4, add_mult_5_cout0, add_mult_5_cout1, add_mult_5_cout2, add_mult_5_cout3,
       add_mult_5_cout4, add_mult_5_out1, add_mult_5_out2, add_mult_5_out3, add_mult_5_out4;

  adder_sub Adder_subtractor (
    .Ci(1'b0), .B4(add_mult_1_cout4), .A4(1'b0), .B3(add_mult_1_cout1), .A3(add_mult_1_out4),
    .B2(add_mult_1_cout2), .A2(add_mult_1_out3), .B1(add_mult_1_cout3), .A1(add_mult_1_out2),
    .B0(add_mult_1_cout0), .A0(add_mult_1_out1), .OUT4(Out_9), .OUT3(Out_8), .OUT2(Out_7), .OUT1(Out_6),
    .OUT0(Out_5));  // open: COUT
  add_mult add_mult_1 (
    .COUT0(add_mult_1_cout0), .COUT3(add_mult_1_cout3), .COUT2(add_mult_1_cout2), .COUT1(add_mult_1_cout1),
    .COUT4(add_mult_1_cout4), .C0(add_mult_2_cout0), .C3(add_mult_2_cout3), .C2(add_mult_2_cout2),
    .C1(add_mult_2_cout1), .C4(add_mult_2_cout4), .B4(B4), .A4(A4), .S4(1'b0), .B3(B4), .A3(A3),
    .S3(add_mult_2_out4), .B2(B4), .A2(A2), .S2(add_mult_2_out3), .B1(B4), .A1(A1), .S1(add_mult_2_out2),
    .B0(B4), .A0(A0), .S0(add_mult_2_out1), .OUT4(add_mult_1_out4), .OUT3(add_mult_1_out3),
    .OUT2(add_mult_1_out2), .OUT1(add_mult_1_out1), .OUT0(Out_4));
  nor nor_1 (ZERO, Out_9, Out_8, Out_7, Out_5, Out_4, Out_3, Out_2, Out_1, Out_6, Out_0);
  add_mult add_mult_2 (
    .COUT0(add_mult_2_cout0), .COUT3(add_mult_2_cout3), .COUT2(add_mult_2_cout2), .COUT1(add_mult_2_cout1),
    .COUT4(add_mult_2_cout4), .C0(add_mult_3_cout0), .C3(add_mult_3_cout3), .C2(add_mult_3_cout2),
    .C1(add_mult_3_cout1), .C4(add_mult_3_cout4), .B4(B3), .A4(A4), .S4(1'b0), .B3(B3), .A3(A3),
    .S3(add_mult_3_out4), .B2(B3), .A2(A2), .S2(add_mult_3_out3), .B1(B3), .A1(A1), .S1(add_mult_3_out2),
    .B0(B3), .A0(A0), .S0(add_mult_3_out1), .OUT4(add_mult_2_out4), .OUT3(add_mult_2_out3),
    .OUT2(add_mult_2_out2), .OUT1(add_mult_2_out1), .OUT0(Out_3));
  add_mult add_mult_3 (
    .COUT0(add_mult_3_cout0), .COUT3(add_mult_3_cout3), .COUT2(add_mult_3_cout2), .COUT1(add_mult_3_cout1),
    .COUT4(add_mult_3_cout4), .C0(add_mult_4_cout0), .C3(add_mult_4_cout3), .C2(add_mult_4_cout2),
    .C1(add_mult_4_cout1), .C4(add_mult_4_cout4), .B4(B2), .A4(A4), .S4(1'b0), .B3(B2), .A3(A3),
    .S3(add_mult_4_out4), .B2(B2), .A2(A2), .S2(add_mult_4_out3), .B1(B2), .A1(A1), .S1(add_mult_4_out2),
    .B0(B2), .A0(A0), .S0(add_mult_4_out1), .OUT4(add_mult_3_out4), .OUT3(add_mult_3_out3),
    .OUT2(add_mult_3_out2), .OUT1(add_mult_3_out1), .OUT0(Out_2));
  add_mult add_mult_4 (
    .COUT0(add_mult_4_cout0), .COUT3(add_mult_4_cout3), .COUT2(add_mult_4_cout2), .COUT1(add_mult_4_cout1),
    .COUT4(add_mult_4_cout4), .C0(add_mult_5_cout0), .C3(add_mult_5_cout3), .C2(add_mult_5_cout2),
    .C1(add_mult_5_cout1), .C4(add_mult_5_cout4), .B4(B1), .A4(A4), .S4(1'b0), .B3(B1), .A3(A3),
    .S3(add_mult_5_out4), .B2(B1), .A2(A2), .S2(add_mult_5_out3), .B1(B1), .A1(A1), .S1(add_mult_5_out2),
    .B0(B1), .A0(A0), .S0(add_mult_5_out1), .OUT4(add_mult_4_out4), .OUT3(add_mult_4_out3),
    .OUT2(add_mult_4_out2), .OUT1(add_mult_4_out1), .OUT0(Out_1));
  add_mult add_mult_5 (
    .COUT0(add_mult_5_cout0), .COUT3(add_mult_5_cout3), .COUT2(add_mult_5_cout2), .COUT1(add_mult_5_cout1),
    .COUT4(add_mult_5_cout4), .C0(1'b0), .C3(1'b0), .C2(1'b0), .C1(1'b0), .C4(1'b0), .B4(B0), .A4(A4),
    .S4(1'b0), .B3(B0), .A3(A3), .S3(1'b0), .B2(B0), .A2(A2), .S2(1'b0), .B1(B0), .A1(A1), .S1(1'b0),
    .B0(B0), .A0(A0), .S0(1'b0), .OUT4(add_mult_5_out4), .OUT3(add_mult_5_out3), .OUT2(add_mult_5_out2),
    .OUT1(add_mult_5_out1), .OUT0(Out_0));
endmodule

module combare (
  input  B0,
  input  B1,
  input  A1,
  input  A0,
  input  A2,
  input  B2,
  input  A3,
  input  B3,
  input  A4,
  input  B4,
  output A__B,
  output Output_is_negative,
  output A__B_2
);

  wire Adder_subtractor_out0, Adder_subtractor_out1, Adder_subtractor_out2, Adder_subtractor_out3,
       Adder_subtractor_out4, nor_1_out;

  not not_1 (Output_is_negative, A__B);
  or or_1 (A__B_2, Output_is_negative, nor_1_out);
  nor nor_1 (nor_1_out, Adder_subtractor_out4, Adder_subtractor_out3, Adder_subtractor_out2, Adder_subtractor_out1, Adder_subtractor_out0);
  adder_sub Adder_subtractor (
    .COUT(A__B), .Ci(1'b1), .B4(B4), .A4(A4), .B3(B3), .A3(A3), .B2(B2), .A2(A2), .B1(B1), .A1(A1), .B0(B0),
    .A0(A0), .OUT4(Adder_subtractor_out4), .OUT3(Adder_subtractor_out3), .OUT2(Adder_subtractor_out2),
    .OUT1(Adder_subtractor_out1), .OUT0(Adder_subtractor_out0));
endmodule

// MUX
module trans_mux (
  input  D0,
  input  D1,
  input  D2,
  input  D3,
  input  S1,
  input  S0,
  output OUTPUT
);

  wire not_1_out, not_2_out, transmission_1_p4, transmission_3_p4;

  not not_1 (not_1_out, S0);
  // Transmission_Gate transmission_1: pin names not known; wires that end beside it: D0, S0, not_1_out, transmission_1_p4
  // Transmission_Gate transmission_2: pin names not known; wires that end beside it: D1, not_1_out, S0, transmission_1_p4
  // Transmission_Gate transmission_3: pin names not known; wires that end beside it: D2, S0, not_1_out, transmission_3_p4
  // Transmission_Gate transmission_4: pin names not known; wires that end beside it: D3, not_1_out, S0, transmission_3_p4
  not not_2 (not_2_out, S1);
  // Transmission_Gate transmission_5: pin names not known; wires that end beside it: transmission_1_p4, S1, not_2_out, OUTPUT
  // Transmission_Gate transmission_6: pin names not known; wires that end beside it: transmission_3_p4, not_2_out, S1, OUTPUT
endmodule

module SMALL_mux (
  input  S1,
  input  S0,
  output mux1,
  output mux0
);

  wire not_1_out, not_2_out;

  and and_1 (mux1, S1, not_1_out);
  not not_1 (not_1_out, S0);
  not not_2 (not_2_out, S1);
  and and_2 (mux0, not_2_out, S0);
endmodule
